# Fritzing sketch 7SegmentIRCounter (saved by Fritzing 0.9.3b)
breadboards: 1

parts:
  Part1 = Intel Galileo Gen2
  DI1 = 7-Segment LED Display [package=THT]
  R1 = Resistor [tolerance=±5% resistance=220 package=THT]
  R2 = Resistor [tolerance=±5% resistance=220 package=THT]
  R3 = Resistor [tolerance=±5% resistance=220 package=THT]
  R4 = Resistor [tolerance=±5% resistance=220 package=THT]
  R5 = Resistor [tolerance=±5% resistance=220 package=THT]
  R6 = Resistor [tolerance=±5% resistance=220 package=THT]
  R7 = Resistor [tolerance=±5% resistance=220 package=THT]
  J1 = Infrared Proximity Sensor

nets:
  N1: Part1.D8, R4.Pin_0
  N2: Part1.D9_PWM, J1.Vout
  N3: Part1.D2, R2.Pin_1
  N4: Part1.D3_PWM, R1.Pin_1
  N5: Part1.D4, R5.Pin_1
  N6: Part1.D5_PWM, R6.Pin_0
  N7: Part1.D6_PWM, R7.Pin_0
  N8: Part1.D7, R3.Pin_0
  5V: Part1.5V, DI1.commAnode, J1.Vcc
  GND: Part1.GND, J1.GND
  N9: DI1.cathodeE, R7.Pin_1
  N10: DI1.cathodeD, R6.Pin_1
  N11: DI1.cathodeC, R5.Pin_0
  N12: DI1.cathodeB, R2.Pin_0
  N13: DI1.cathodeA, R1.Pin_0
  N14: DI1.cathodeF, R3.Pin_1
  N15: DI1.cathodeG, R4.Pin_1
